# Fritzing sketch LedPcb (saved by Fritzing 0.9.3b)
circuit board: 4.37623cm x 4.9483cm
breadboards: 1

parts:
  J7 = female pin header, 3 pins [form="♀ (female)"]
  J6 = female pin header, 3 pins [form="♀ (female)"]
  J8 = shrouded pin header, 10 pins [form="♂ (shrouded male)"]

nets:
  N1: J7.pin1, J8.pin6
  N2: J7.pin2, J8.pin7
  N3: J7.pin3, J8.pin8
  N4: J6.pin1, J8.pin5
  N5: J6.pin2, J8.pin4
  N6: J6.pin3, J8.pin3
